# Fritzing sketch Chapter_10_Diagram (saved by Fritzing 0.9.3b)
breadboards: 1

parts:
  Part1 = Arduino Uno (Rev3)
  SONAR1 = Maxbotix MaxSonar Ultrasonic Sensor (Hi-Res)
  M1 = fc-51 [package=THT]
  S1 = Toggle Switch [package=THT]
  R1 = Resistor [tolerance=±5% resistance=4.7k package="1206 [SMD]"]

nets:
  N1: Part1.A1, SONAR1.AN
  N2: Part1.D3_PWM, M1.pin1
  N3: Part1.D4, S1.Ground, R1.Pin_0
  5V: Part1.5V, SONAR1.+5V, M1.pin3, S1.5V, R1.Pin_1
  GND: Part1.GND, SONAR1.GND, M1.pin2, S1.Out

custom parts:
  Maxbotix MaxSonar Ultrasonic Sensor (Hi-Res): Maxbotix MaxSonar Hi-Resolution Ultrasonic Sensor HRLV-EZ0, HRLV-EZ1, HRLV-EZ2, HRLV-EZ3, HRLV-EZ4
  Toggle Switch: Crash Sensor
