# Fritzing sketch RGBLED (saved by Fritzing 0.9.3b)
breadboards: 1

parts:
  R2 = Resistor [tolerance=±5% resistance=330 package=THT]
  R3 = Resistor [tolerance=±5% resistance=330 package=THT]
  R4 = Resistor [tolerance=±5% resistance=330 package=THT]
  LED1 = RGB LED - (4 legs) [package="5 mm [THT]"]
  Part1 = Arduino Uno (Rev3)

nets:
  N1: R2.Pin_0, LED1.common_anode
  N2: R2.Pin_1, Part1.D10_PWM/SS
  N3: R3.Pin_0, LED1.blue_cathode
  N4: R3.Pin_1, Part1.D11_PWM/MOSI
  N5: R4.Pin_0, LED1.red_cathode
  N6: R4.Pin_1, Part1.D9_PWM
