# Fritzing sketch Chapter 12  (saved by Fritzing 0.9.3b)
breadboards: 1

parts:
  Part1 = Arduino Uno (Rev3)
  SP1 = SPEAKER [package=pcb_mount_speaker]
  J1 = Piezo Speaker

nets:
  N1: Part1.D8, J1.pin2
  N2: Part1.D7, SP1.-
  N3: Part1.GND, SP1.+, J1.pin1
