# Fritzing sketch Chapter 14 (saved by Fritzing 0.9.3b)
breadboards: 1

parts:
  Part2 = Arduino Uno (Rev3)
  DHT2 = DHT11 Humitidy and Temperature Sensor
  R2 = Resistor [tolerance=±5% resistance=4.7k package=THT]

nets:
  N1: Part2.D3_PWM, DHT2.DATA, R2.Pin_0
  5V: Part2.5V, DHT2.VDD, R2.Pin_1
  GND: Part2.GND, DHT2.GND

custom parts:
  DHT11 Humitidy and Temperature Sensor: DHT11 Humidity and Temperature Sensor
