# Fritzing sketch L293D (saved by Fritzing 0.9.3b)
breadboards: 1

parts:
  Part2 = Arduino Uno (Rev3)
  IC1 = L293D [package=THT]
  M2 = DC Motor
  VCC1 = Battery block 9V

nets:
  N1: Part2.D10_PWM/SS, IC1.Enable_1
  N2: Part2.D2, IC1.In_2
  N3: Part2.D3_PWM, IC1.In_1
  N4: Part2.GND, IC1.0V, VCC1.-
  N5: IC1.Out_1_(_Controlled_by_Enable_1_), M2.pin_2
  N6: IC1.Out_2_(_Controlled_by_Enable_1_), M2.pin_1
  N7: IC1.+Vmotor, VCC1.+
