# Fritzing sketch L298N (saved by Fritzing 0.9.3b)
breadboards: 1

parts:
  Part1 = Arduino Uno (Rev3)
  S1 = H-Bridge with L298N
  M1 = DC Motor
  VCC1 = Battery block 9V

nets:
  N1: Part1.D10_PWM/SS, S1.ENA
  N2: Part1.D2, S1.IN2
  N3: Part1.D3_PWM, S1.IN1
  GND: Part1.GND, S1.GND, VCC1.-
  N4: S1.12V, VCC1.+
  N5: S1.M1-01, M1.pin_2
  N6: S1.M1-02, M1.pin_1

custom parts:
  H-Bridge with L298N: h-bridge
