# Fritzing sketch Chapter 16 (saved by Fritzing 0.9.3b)
breadboards: 1

parts:
  Part1 = Arduino Uno (Rev3)
  U1 = POT [package=trim_pot]
  J1 = Basic Servo
  VCC1 = 4 x AAA Battery Mount

nets:
  N1: Part1.A0, U1.E
  N2: Part1.D3_PWM, J1.pulse
  N3: Part1.5V, U1.S
  GND: Part1.GND, U1.A, J1.gnd, VCC1.-
  N4: J1.vcc, VCC1.+
