# Fritzing sketch Blinking Lamp (saved by Fritzing 0.9.3b)

parts:
  LED1 = LEDs [package=led10mm]
  KY-1 = Keyes Relay [package=THT]
  Part1 = Arduino Uno (Rev3)

nets:
  N1: LED1.C, KY-1.NO
  N2: KY-1.signal, Part1.D3_PWM
  N3: KY-1.power, Part1.5V
  N4: KY-1.ground, Part1.GND

notes:
  Plugs into wall outlet

custom parts:
  LEDs: LEDs Standard schematic elements and footprints for 5mm, 3mm, 1206, and 0603 sized LEDs. 5mm - Spark Fun Electronics SKU : COM-00529 (and others)
  Keyes Relay: The Keyes 5V relay module is suitable for SCM development, home appliance control. It uses a 5V~12V TIL control signal which can control DC / AC signal.
