# Fritzing sketch Motor (saved by Fritzing 0.9.3b)

parts:
  Part2 = Arduino Uno (Rev3)
  KY-2 = Keyes Relay [package=THT]
  VCC1 = Battery block 9V
  M1 = DC Motor

nets:
  N1: Part2.D3_PWM, KY-2.signal
  N2: Part2.5V, KY-2.power
  N3: Part2.GND, KY-2.ground
  N4: KY-2.C, M1.pin_1
  N5: KY-2.NO, VCC1.+

custom parts:
  Keyes Relay: The Keyes 5V relay module is suitable for SCM development, home appliance control. It uses a 5V~12V TIL control signal which can control DC / AC signal.
