# Fritzing sketch Chapter21 (saved by Fritzing 0.9.3b)
breadboards: 1

parts:
  Part1 = Arduino Uno (Rev3)
  Part2 = Arduino Uno (Rev3)
  BT1 = Bluetooth HC-06u [package=THT]
  BT2 = Bluetooth HC-06u [package=THT]
  Part3 = Thumb Joystick

nets:
  N1: Part1.A0, Part3.HORZ
  N2: Part1.A1, Part3.VERT
  N3: Part1.D10_PWM/SS, BT1.RXD
  N4: Part1.D11_PWM/MOSI, BT1.TXD
  N5: Part1.D2, Part3.SEL
  VCC: Part1.5V, BT1.VCC, Part3.VCC
  GND: Part1.GND, BT1.GND, Part3.GND
  N6: Part2.D10_PWM/SS, BT2.RXD
  N7: Part2.D11_PWM/MOSI, BT2.TXD
  GND_2: Part2.GND, BT2.GND

custom parts:
  Bluetooth HC-06u: Bluetooth HC-06 - face up, pins down 16.5mm x 37.5mm PCB
