# Fritzing sketch Chapter_9_diagram (saved by Fritzing 0.9.3b)
breadboards: 1

parts:
  Part1 = Arduino Uno (Rev3)
  DHT1 = DHT11 Humitidy and Temperature Sensor
  YL-83_-_Control_Board1 = YL-83 Rain Sensor - Control Board
  YL-83_-_Detection_Board1 = YL-83 Rain Sensor - Detection Board
  R1 = Resistor [tolerance=±5% resistance=4.7k package=THT]

nets:
  N1: Part1.A2, YL-83_-_Control_Board1.AO
  N2: Part1.D3_PWM, DHT1.DATA, R1.Pin_0
  5V: Part1.5V, DHT1.VDD, YL-83_-_Control_Board1.VCC, R1.Pin_1
  GND: Part1.GND, DHT1.GND, YL-83_-_Control_Board1.GND
  N3: YL-83_-_Control_Board1.POS, YL-83_-_Detection_Board1.NEG
  N4: YL-83_-_Control_Board1.NEG, YL-83_-_Detection_Board1.POS

custom parts:
  DHT11 Humitidy and Temperature Sensor: DHT11 Humidity and Temperature Sensor
  YL-83 Rain Sensor - Control Board: The YL-83 is a rain sensor that has more resistance when dry and less resistance when wet. The module runs at 5V.
  YL-83 Rain Sensor - Detection Board: The YL-83 is a rain sensor that has more resistance when dry and less resistance when wet. The module runs at 5V.
